// Logisim project minicomputer.circ as structural Verilog: 12 circuits, main circuit main
module main (
  input  [7:0] in_1
);

  Clock clock_1 ();  // open: out
  datapath datapath_1 ();

  // Notes on the sheet:
  //   big_endian
endmodule

module datapath (
);

  st_bit_register st_bit_register_1 ();  // open: DATA, clear, store, clk, REC
  ALU alu_1 ();  // open: D1, D2, zero, control, SIG_OUT, R1, R2
endmodule

module data_memory (
);

  Register register_1 ();  // open: D, en, clk, Q, clr
endmodule

module instruction_memory (
);

  Register register_1 ();  // open: D, en, clk, Q, clr
endmodule

module st_bit_register (
  input  [15:0] DATA,
  input  clear,
  input  store,
  input  clk,
  output [15:0] REC
);

  wire [15:0] multiplexer_1_out;

  Multiplexer #(.width(16)) multiplexer_1 (.in0(DATA), .in1(REC), .out(multiplexer_1_out), .sel(store));
  eight_bit_register eight_bit_register_1 (.in_1(multiplexer_1_out[15:8]), .clear(clear), .clk(clk), .R(REC[15:8]));
  eight_bit_register eight_bit_register_2 (.in_1(multiplexer_1_out[7:0]), .clear(clear), .clk(clk), .R(REC[7:0]));
endmodule

module eight_bit_register (
  input  [7:0] in_1,
  input  clear,
  input  clk,
  output [7:0] R
);

  flipflop_d flipflop_d_1 (.D(in_1[0]), .clear(clear), .clk(clk), .Q(R[0]));
  flipflop_d flipflop_d_2 (.D(in_1[7]), .clear(clear), .clk(clk), .Q(R[7]));
  flipflop_d flipflop_d_3 (.D(in_1[1]), .clear(clear), .clk(clk), .Q(R[1]));
  flipflop_d flipflop_d_4 (.D(in_1[6]), .clear(clear), .clk(clk), .Q(R[6]));
  flipflop_d flipflop_d_5 (.D(in_1[2]), .clear(clear), .clk(clk), .Q(R[2]));
  flipflop_d flipflop_d_6 (.D(in_1[5]), .clear(clear), .clk(clk), .Q(R[5]));
  flipflop_d flipflop_d_7 (.D(in_1[3]), .clear(clear), .clk(clk), .Q(R[3]));
  flipflop_d flipflop_d_8 (.D(in_1[4]), .clear(clear), .clk(clk), .Q(R[4]));
endmodule

module flipflop_d (
  input  D,
  input  clear,
  input  clk,
  output Q
);

  wire master_latch_q, not_1_out;

  not not_1 (not_1_out, clk);
  latch_d master_latch (.D(D), .reset(clear), .E(not_1_out), .Q(master_latch_q));  // open: NQ
  latch_d slave_latch (.D(master_latch_q), .reset(clear), .E(clk), .Q(Q));  // open: NQ
endmodule

module latch_d (
  input  D,
  input  reset,
  input  E,
  output Q,
  output NQ
);

  wire nand_1_out, nand_2_out, not_1_out, not_2_out;

  not not_1 (not_1_out, D);
  nand nand_1 (nand_1_out, D, E);
  nand nand_2 (nand_2_out, E, not_1_out);
  not not_2 (not_2_out, reset);
  nand nand_3 (Q, nand_1_out, NQ);
  nand nand_4 (NQ, Q, not_2_out, nand_2_out);
endmodule

module ALU (
  input  [15:0] D1,
  input  [15:0] D2,
  input  [15:0] zero,
  input  [2:0] control,
  output SIG_OUT,
  output [15:0] R1,
  output [15:0] R2
);

  wire comparator_1_eq, LSA_carry_out, MSA_carry_out, subtractor_1_bout;
  wire [7:0] LSA_out_4, MSA_out_4;
  wire [15:0] divider_1_out, divider_1_rem, multiplier_1_cout, multiplier_1_out, negator_1_out,
       shifter_1_out, subtractor_1_out;

  eight_bit_adder LSA (.in_1(1'b0), .D1(D1[7:0]), .D2(D2[7:0]), .out_4(LSA_out_4), .carry_out(LSA_carry_out));
  eight_bit_adder MSA (
    .in_1(LSA_carry_out), .D1(D1[15:8]), .D2(D2[15:8]), .out_4(MSA_out_4), .carry_out(MSA_carry_out));
  Subtractor #(.width(16)) subtractor_1 (.a(D1), .b(D2), .out(subtractor_1_out), .bin(1'b0), .bout(subtractor_1_bout));
  Multiplier #(.width(16)) multiplier_1 (
    .a(D1), .b(D2), .out(multiplier_1_out), .cout(multiplier_1_cout));  // open: cin
  Divider #(.width(16)) divider_1 (.a(D1), .b(D2), .out(divider_1_out), .rem(divider_1_rem));  // open: upper
  Comparator #(.width(16)) comparator_1 (.a(D1), .b(D2), .eq(comparator_1_eq));  // open: gt, lt
  Negator #(.width(16)) negator_1 (.in(D1), .out(negator_1_out));
  Shifter #(.width(16)) shifter_1 (.in(D1), .\dist (D2[3:0]), .out(shifter_1_out));
  Multiplexer #(.select(3), .width(16)) multiplexer_1 (
    .in0(zero), .in1({MSA_out_4, LSA_out_4}), .in2(subtractor_1_out), .in3(multiplier_1_out),
    .in4(divider_1_out), .in5(zero), .in6(negator_1_out), .in7(shifter_1_out), .out(R1), .sel(control));
  Multiplexer #(.select(3)) multiplexer_2 (
    .in0(1'b0), .in1(MSA_carry_out), .in2(subtractor_1_bout), .in3(1'b0), .in4(1'b0), .in5(comparator_1_eq),
    .in6(1'b0), .in7(1'b0), .out(SIG_OUT), .sel(control));
  Multiplexer #(.select(3), .width(16)) multiplexer_3 (
    .in0(zero), .in1(zero), .in2(zero), .in3(multiplier_1_cout), .in4(divider_1_rem), .in5(zero), .in6(zero),
    .in7(zero), .out(R2), .sel(control));

  // Notes on the sheet:
  //   sub
  //   mult
  //   div
  //   add
  //   carry out
  //   borrow out
  //   equal
  //   neg
  //   shift
endmodule

module eight_bit_adder (
  input  in_1,
  input  [7:0] D1,
  input  [7:0] D2,
  output [7:0] out_4,
  output carry_out
);

  wire full_adder_1_co, full_adder_2_co, full_adder_3_co, full_adder_4_co, full_adder_5_co, full_adder_6_co,
       full_adder_7_co;

  full_adder full_adder_1 (.A(D1[0]), .B(D2[0]), .CI(in_1), .CO(full_adder_1_co), .S(out_4[0]));
  full_adder full_adder_2 (.A(D1[4]), .B(D2[4]), .CI(full_adder_7_co), .CO(full_adder_2_co), .S(out_4[4]));
  full_adder full_adder_3 (.A(D1[1]), .B(D2[1]), .CI(full_adder_1_co), .CO(full_adder_3_co), .S(out_4[1]));
  full_adder full_adder_4 (.A(D1[5]), .B(D2[5]), .CI(full_adder_2_co), .CO(full_adder_4_co), .S(out_4[5]));
  full_adder full_adder_5 (.A(D1[2]), .B(D2[2]), .CI(full_adder_3_co), .CO(full_adder_5_co), .S(out_4[2]));
  full_adder full_adder_6 (.A(D1[6]), .B(D2[6]), .CI(full_adder_4_co), .CO(full_adder_6_co), .S(out_4[6]));
  full_adder full_adder_7 (.A(D1[3]), .B(D2[3]), .CI(full_adder_5_co), .CO(full_adder_7_co), .S(out_4[3]));
  full_adder full_adder_8 (.A(D1[7]), .B(D2[7]), .CI(full_adder_6_co), .CO(carry_out), .S(out_4[7]));

  // Notes on the sheet:
  //   result
endmodule

module full_adder (
  input  A,
  input  B,
  input  CI,
  output CO,
  output S
);

  wire half_adder_1_c, half_adder_1_s, half_adder_2_c;

  half_adder half_adder_1 (.A(A), .B(B), .C(half_adder_1_c), .S(half_adder_1_s));
  half_adder half_adder_2 (.A(half_adder_1_s), .B(CI), .C(half_adder_2_c), .S(S));
  or or_1 (CO, half_adder_1_c, half_adder_2_c);
endmodule

module half_adder (
  input  A,
  input  B,
  output C,
  output S
);

  and and_1 (C, A, B);
  xor xor_1 (S, A, B);
endmodule
