// Logisim project architecture.circ as structural Verilog: 7 circuits, main circuit main
module main (
);

  wire clock_1_out, datapath_1_readmemory, datapath_1_writememory;
  wire [15:0] bus_control_output_data, datapath_1_memory_address, datapath_1_memory_output;

  Clock clock_1 (.out(clock_1_out));
  datapath datapath_1 (
    .memory_input(bus_control_output_data), .clk(clock_1_out), .memory_address(datapath_1_memory_address),
    .memory_output(datapath_1_memory_output), .writeMemory(datapath_1_writememory),
    .readMemory(datapath_1_readmemory));  // open: reset
  memory bus_control (
    .memory_address(datapath_1_memory_address), .input_data(datapath_1_memory_output),
    .write(datapath_1_writememory), .load(datapath_1_readmemory), .clk(clock_1_out),
    .output_data(bus_control_output_data));
endmodule

module datapath (
  input  [15:0] memory_input,
  input  reset,
  input  clk,
  output [15:0] memory_address,
  output [15:0] memory_output,
  output writeMemory,
  output readMemory
);

  wire ALU_out, Immediate_out, MDR_out, PC_out, priority_encoder_1_en_out, weReg;
  wire [1:0] priority_encoder_1_out, sourcePC;
  wire [2:0] ALUop, writeRegAddr;
  wire [3:0] ALUflags;
  wire [4:0] control_unit_1_we_control;
  wire [5:0] readRegsAddr;
  wire [15:0] adder_1_out, ALUResult, currentInstruction, currentInstructionAddr, dataBus, immediateValue,
       IR_q, multiplexer_3_out, nextInstructionAddr, registers_database_1_r1, registers_database_1_r2,
       stackInstructionAddr;

  control_unit control_unit_1 (
    .instruction(IR_q), .ALUflags(ALUflags), .freeze(1'b0), .reset(reset), .clk(clk),
    .immediate(immediateValue), .reg_write(writeRegAddr), .reg_read_A(readRegsAddr[2:0]),
    .reg_read_B(readRegsAddr[5:3]), .mem_control({writeMemory, readMemory}), .pcSource(sourcePC),
    .ALU_op(ALUop), .we_control({weReg, control_unit_1_we_control}),
    .out_control({Immediate_out, ALU_out, MDR_out, PC_out}));
  Register #(.width(16)) IR (
    .D(currentInstruction), .en(control_unit_1_we_control[0]), .clk(clk), .Q(IR_q), .clr(reset));
  Register #(.width(16)) PC (
    .D(nextInstructionAddr), .en(control_unit_1_we_control[1]), .clk(clk), .Q(currentInstructionAddr),
    .clr(reset));
  Register #(.width(16)) SP (
    .D(dataBus), .en(control_unit_1_we_control[2]), .clk(clk), .Q(stackInstructionAddr), .clr(reset));
  Register #(.width(16)) MAR (
    .D(currentInstructionAddr), .en(control_unit_1_we_control[3]), .clk(clk), .Q(memory_address), .clr(reset));
  Register #(.width(16)) MDR (
    .D(memory_input), .en(control_unit_1_we_control[4]), .clk(clk), .Q(currentInstruction), .clr(reset));
  Adder #(.width(16)) adder_1 (.a(16'h1), .b(currentInstructionAddr), .out(adder_1_out));  // open: cin, cout
  Priority_Encoder #(.select(2)) priority_encoder_1 (
    .in0(PC_out), .in1(MDR_out), .in2(ALU_out), .in3(Immediate_out), .out(priority_encoder_1_out),
    .en_out(priority_encoder_1_en_out), .en_in(1'b1));  // open: gs
  Multiplexer #(.select(2), .width(16)) multiplexer_1 (
    .in0(adder_1_out), .in1(immediateValue), .in2(stackInstructionAddr), .in3(ALUResult),
    .out(nextInstructionAddr), .sel(sourcePC));
  registers_database registers_database_1 (
    .DATA(dataBus), .write(weReg), .rReg1_addr(readRegsAddr[2:0]), .rReg2_addr(readRegsAddr[5:3]),
    .wReg_addr(writeRegAddr), .clk(clk), .R1(registers_database_1_r1), .R2(registers_database_1_r2));
  Multiplexer #(.select(2), .width(16)) multiplexer_2 (
    .in0(nextInstructionAddr), .in1(currentInstruction), .in2(ALUResult), .in3(immediateValue),
    .out(dataBus), .sel(priority_encoder_1_out));
  Multiplexer #(.width(16)) multiplexer_3 (
    .in0(registers_database_1_r2), .in1(immediateValue), .out(multiplexer_3_out), .sel(Immediate_out));
  ALU alu_1 (
    .D1(registers_database_1_r1), .D2(multiplexer_3_out), .opControl(ALUop), .ALUflags(ALUflags),
    .Res1(ALUResult));  // open: carryIn, Res2
  // also tied to VCC on the sheet: priority_encoder_1_en_out

  // Other names for the same wires on the sheet: readMem = readMemory; writeMem = writeMemory; clock = clk;
  //   memoryAddressOut[15:0] = memory_address; memoryDataIn[15:0] = memory_input; memoryDataOut[15:0] = memory_output
endmodule

module ALU (
  input  [15:0] D1,
  input  [15:0] D2,
  input  [15:0] carryIn,
  input  [2:0] opControl,
  output [15:0] Res1,
  output [15:0] Res2,
  output [3:0] ALUflags
);

  wire addOverflow, borrowOut, carryOut, not_1_out, not_2_out, subOverflow, xor_1_out, xor_2_out, xor_3_out,
       xor_4_out;
  wire [15:0] adder_1_out, and_3_out, divider_1_out, divRemain, multCarryOut, multiplier_1_out, or_1_out,
       shifter_1_out, shifter_2_out, subtractor_1_out;

  Adder #(.width(16)) adder_1 (.a(D1), .b(D2), .out(adder_1_out), .cin(carryIn[0]), .cout(carryOut));
  Subtractor #(.width(16)) subtractor_1 (.a(D1), .b(D2), .out(subtractor_1_out), .bin(carryIn[0]), .bout(borrowOut));
  Multiplier #(.width(16)) multiplier_1 (.a(D1), .b(D2), .out(multiplier_1_out), .cin(carryIn), .cout(multCarryOut));
  Divider #(.width(16)) divider_1 (.a(D1), .b(D2), .out(divider_1_out), .upper(carryIn), .rem(divRemain));
  Shifter #(.shift("lr"), .width(16)) shifter_1 (.in(D1), .\dist (D2[3:0]), .out(shifter_1_out));
  Shifter #(.width(16)) shifter_2 (.in(D1), .\dist (D2[3:0]), .out(shifter_2_out));
  not not_1 (not_1_out, xor_1_out);
  xor xor_1 (xor_1_out, D1[15], D2[15]);
  xor xor_2 (xor_2_out, D1[15], ALUflags[1]);
  xor xor_3 (xor_3_out, D1[15], D2[15]);
  xor xor_4 (xor_4_out, D1[15], ALUflags[1]);
  and and_1 (addOverflow, not_1_out, xor_2_out);
  and and_2 (subOverflow, xor_3_out, xor_4_out);
  assign and_3_out = D2 & D1;  // AND_Gate and_3, 16 bits wide
  assign or_1_out = D2 | D1;  // OR_Gate or_1, 16 bits wide
  not not_2 (not_2_out, borrowOut);
  Multiplexer #(.select(3), .width(16)) multiplexer_1 (
    .in0(adder_1_out), .in1(subtractor_1_out), .in2(multiplier_1_out), .in3(divider_1_out), .in4(and_3_out),
    .in5(or_1_out), .in6(shifter_1_out), .in7(shifter_2_out), .out({ALUflags[1], Res1[14:0]}), .sel(opControl));
  Multiplexer #(.select(3), .width(16)) multiplexer_2 (
    .in0({16{1'b0}}), .in1({16{1'b0}}), .in2(multCarryOut), .in3(divRemain), .in4({16{1'b0}}),
    .in5({16{1'b0}}), .in6({16{1'b0}}), .in7({16{1'b0}}), .out(Res2), .sel(opControl));
  Multiplexer #(.select(3)) multiplexer_3 (
    .in0(carryOut), .in1(not_2_out), .in2(1'b0), .in3(1'b0), .in4(1'b0), .in5(1'b0), .in6(1'b0), .in7(1'b0),
    .out(ALUflags[2]), .sel(opControl));
  Multiplexer #(.select(3)) multiplexer_4 (
    .in0(addOverflow), .in1(subOverflow), .in2(1'b0), .in3(1'b0), .in4(1'b0), .in5(1'b0), .in6(1'b0),
    .in7(1'b0), .out(ALUflags[3]), .sel(opControl));
  nor nor_1 (ALUflags[0], Res1[7], Res1[0], Res1[1], Res1[2], Res1[3], Res1[4], Res1[5], Res1[6], Res1[8], Res1[9], Res1[10], Res1[11], Res1[12], Res1[13], Res1[14], ALUflags[1]);

  assign Res1[15] = ALUflags[1];

  // Other names for the same wires on the sheet: flagZero = ALUflags[0]; flagCarry = ALUflags[2];
  //   flagOverflow = ALUflags[3]; A = D1[15]; B = D2[15]; flagNegative = ALUflags[1]; R = ALUflags[1]

  // Notes on the sheet:
  //   sub
  //   mult
  //   div
  //   add
  //   or
  //   and
  //   shft_r
  //   shift_l
endmodule

module control_unit (
  input  [15:0] instruction,
  input  [3:0] ALUflags,
  input  freeze,
  input  reset,
  input  clk,
  output [15:0] immediate,
  output [2:0] reg_write,
  output [2:0] reg_read_A,
  output [2:0] reg_read_B,
  output [1:0] mem_control,
  output [1:0] pcSource,
  output [2:0] ALU_op,
  output [5:0] we_control,
  output [3:0] out_control
);

  wire weState;
  wire [2:0] control_decoder_1_next_state, StateRegister_q;

  not not_1 (weState, freeze);
  Multiplexer #(.width(3)) multiplexer_1 (.in0(instruction[9:7]), .in1(3'b000), .out(reg_read_A), .sel(out_control[3]));
  Multiplexer #(.width(3)) multiplexer_2 (.in0(instruction[15:13]), .in1(3'b000), .out(ALU_op), .sel(out_control[2]));
  Multiplexer #(.width(3)) multiplexer_3 (.in0(instruction[6:4]), .in1(3'b000), .out(reg_write), .sel(we_control[5]));
  Multiplexer #(.width(3)) multiplexer_4 (
    .in0(instruction[12:10]), .in1(3'b000), .out(reg_read_B), .sel(out_control[3]));
  Multiplexer #(.width(9)) multiplexer_5 (
    .in0({9{1'b0}}), .in1(instruction[15:7]), .out(immediate[8:0]), .sel(out_control[3]));
  Register #(.width(3)) StateRegister (
    .D(control_decoder_1_next_state), .en(weState), .clk(clk), .Q(StateRegister_q), .clr(reset));
  control_decoder control_decoder_1 (
    .state(StateRegister_q), .opcode(instruction[3:0]), .ALU_flags(ALUflags),
    .next_state(control_decoder_1_next_state),
    .signals({out_control, mem_control[0], mem_control[1], we_control[5], we_control[0], we_control[4:1], pcSource}));

  assign immediate[15:9] = {7{1'b0}};

  // Other names for the same wires on the sheet: sourcePC[1:0] = pcSource; loadPC = we_control[1];
  //   loadSP = we_control[2]; loadMAR = we_control[3]; loadMDR = we_control[4]; loadIR = we_control[0];
  //   weReg = we_control[5]; memRead = mem_control[1]; memWrite = mem_control[0]; PC_out = out_control[0];
  //   MDR_out = out_control[1]; ALU_out = out_control[2]; Immediate_out = out_control[3]; ALUoperation[2:0] = ALU_op;
  //   clock = clk; flagsALU[3:0] = ALUflags; flagZero = ALUflags[0]; flagNegative = ALUflags[1];
  //   flagCarry = ALUflags[2]; flagOverflow = ALUflags[3]; immediate16b[8:0] = immediate[8:0];
  //   opcode[3:0] = instruction[3:0]; rt[2:0] = instruction[6:4]; immediateValue[8:0] = instruction[15:7];
  //   rs1[2:0] = instruction[9:7]; rs2[2:0] = instruction[12:10]; aluop[2:0] = instruction[15:13];
  //   read_RegA[2:0] = reg_read_A; read_RegB[2:0] = reg_read_B; write_Reg[2:0] = reg_write

  // Notes on the sheet:
  //   States
  //   Reset: restart the FSM
  //   Fetch2: read instruction data on memory
  //   Decode: decode stored instruction
  //   Execute: execute stored instruction
  //   Memory: read or write data on memory
  //   WriteBack: store the result on a register
  //   Fetch1: search next instruction on memory by address
  //   Fetch3: store instruction and increment next instruction
endmodule

module control_decoder (
  input  [2:0] state,
  input  [3:0] opcode,
  input  [3:0] ALU_flags,
  output [2:0] next_state,
  output [13:0] signals
);

  ROM #(.addrWidth(11), .dataWidth(3)) stateROM (.addr({ALU_flags, opcode, state}), .data(next_state));
  ROM #(.addrWidth(3), .dataWidth(14)) controlROM (.addr(state), .data(signals));

  // Other names for the same wires on the sheet: nextState[2:0] = next_state; currentState[2:0] = state;
  //   romAddr[10:0] = {ALU_flags, opcode, state}; flagsALU[3:0] = ALU_flags; romSignals[13:0] = signals

  // Notes on the sheet:
  //   Moore FSM: outputs depends only by current state
endmodule

module memory (
  input  [15:0] memory_address,
  input  [15:0] input_data,
  input  write,
  input  load,
  input  clk,
  output [15:0] output_data
);

  RAM #(.addrWidth(16), .dataWidth(16)) ram_memory (
    .addr(memory_address), .we(write), .oe(load), .clk(clk), .din(input_data), .dout(output_data));

  // Notes on the sheet:
  //   order: big_endian
endmodule

module registers_database (
  input  [15:0] DATA,
  input  write,
  input  [2:0] rReg1_addr,
  input  [2:0] rReg2_addr,
  input  [2:0] wReg_addr,
  input  clk,
  output [15:0] R1,
  output [15:0] R2
);

  wire decoder_1_out0, decoder_1_out1, decoder_1_out2, decoder_1_out3, decoder_1_out4, decoder_1_out5,
       decoder_1_out6, decoder_1_out7;
  wire [15:0] register_1_q, register_2_q, register_3_q, register_4_q, register_5_q, register_6_q,
       register_7_q, register_8_q;

  Decoder #(.select(3)) decoder_1 (
    .out0(decoder_1_out0), .out1(decoder_1_out1), .out2(decoder_1_out2), .out3(decoder_1_out3),
    .out4(decoder_1_out4), .out5(decoder_1_out5), .out6(decoder_1_out6), .out7(decoder_1_out7),
    .sel(wReg_addr), .en(write));
  Register #(.width(16)) register_1 (.D(DATA), .en(decoder_1_out0), .clk(clk), .Q(register_1_q));  // open: clr
  Register #(.width(16)) register_2 (.D(DATA), .en(decoder_1_out4), .clk(clk), .Q(register_2_q));  // open: clr
  Register #(.width(16)) register_3 (.D(DATA), .en(decoder_1_out1), .clk(clk), .Q(register_3_q));  // open: clr
  Register #(.width(16)) register_4 (.D(DATA), .en(decoder_1_out5), .clk(clk), .Q(register_4_q));  // open: clr
  Register #(.width(16)) register_5 (.D(DATA), .en(decoder_1_out2), .clk(clk), .Q(register_5_q));  // open: clr
  Register #(.width(16)) register_6 (.D(DATA), .en(decoder_1_out6), .clk(clk), .Q(register_6_q));  // open: clr
  Register #(.width(16)) register_7 (.D(DATA), .en(decoder_1_out3), .clk(clk), .Q(register_7_q));  // open: clr
  Register #(.width(16)) register_8 (.D(DATA), .en(decoder_1_out7), .clk(clk), .Q(register_8_q));  // open: clr
  Multiplexer #(.select(3), .width(16)) multiplexer_1 (
    .in0(register_1_q), .in1(register_3_q), .in2(register_5_q), .in3(register_7_q), .in4(register_2_q),
    .in5(register_4_q), .in6(register_6_q), .in7(register_8_q), .out(R1), .sel(rReg1_addr));
  Multiplexer #(.select(3), .width(16)) multiplexer_2 (
    .in0(register_1_q), .in1(register_3_q), .in2(register_5_q), .in3(register_7_q), .in4(register_2_q),
    .in5(register_4_q), .in6(register_6_q), .in7(register_8_q), .out(R2), .sel(rReg2_addr));
endmodule
